# Fritzing sketch Spirit_Proton_Pack (saved by Fritzing 0.9.3b)
breadboards: 1

parts:
  Part3 = NeoPixel Stick [part_number=1426]
  Part4 = NeoPixel Stick [part_number=1426]
  Part9 = Arduino Nano (Rev3.0)
  VCC1 = 4 x AAA Battery Mount
  Part10 = Adafruit Breadboard-Friendly NeoPixel [part_number="Adafruit #1312"]
  Part11 = Adafruit Breadboard-Friendly NeoPixel [part_number="Adafruit #1312"]
  Part12 = Adafruit Breadboard-Friendly NeoPixel [part_number="Adafruit #1312"]
  Part13 = Adafruit Breadboard-Friendly NeoPixel [part_number="Adafruit #1312"]

nets:
  GND: Part3.GND, Part4.GND, Part9.GND, VCC1.-, Part10.GND, Part11.GND, Part12.GND, Part13.GND
  N1: Part3.DATAOUT, Part4.DATAIN
  VDD: Part3.+5V, Part4.+5V, Part10.VDD, Part11.VDD, Part12.VDD, Part13.VDD
  N2: Part3.DATAIN, Part9.D2
  N3: Part9.D3, Part10.IN
  N4: Part9.VIN, VCC1.+
  N5: Part10.OUT, Part11.IN
  N6: Part11.OUT, Part12.IN
  N7: Part12.OUT, Part13.IN

custom parts:
  NeoPixel Stick: Make your own little LED strip arrangement with this stick of NeoPixel LEDs. We crammed 8 of the tiny 5050 (5mm x 5mm) smart RGB LEDs onto a PCB with mounting holes and a chainable design. Use only one microcontroller pin to control as many as you can chain together! Each LED is addressable as the driver chip is inside the LED. Each one has ~18mA constant current drive so the color will be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
  Adafruit Breadboard-Friendly NeoPixel: This is the easiest way possible to add small, bright RGB pixels to your project. We took the same technology from our Flora NeoPixels and made them breadboard friendly, with two rows of 3 x 0.1" spaced header on each side for easy soldering, chaining and breadboarding. These ultra-bright LEDs have a constant-current driver cooked right into the LED package! The pixels are chainable - so you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
