# Fritzing sketch proton_pack_no_bargraph (saved by Fritzing 0.9.3b)
breadboards: 3

parts:
  MP1584EN_Board1 = MP1584EN Power Regulator Board [part_number=MP1584EN]
  MP1584EN_Board2 = MP1584EN Power Regulator Board [part_number=MP1584EN]
  U1 = LIPO-2000mAh [package=lipo-2000]
  Part2 = Audio FX Sound Board
  Part1 = Adafruit Stereo 2.8W Class D Audio Amplifier - I2C Control AGC - TPA2016 [part_number="Adafruit #1712"]
  Part3 = NeoPixel Stick [part_number=1426]
  Part4 = NeoPixel Stick [part_number=1426]
  Part5 = NeoPixel Jewel [part_number=2226]
  Part6 = NeoPixel Jewel [part_number=2226]
  Part7 = NeoPixel Jewel [part_number=2226]
  Part8 = NeoPixel Jewel [part_number=2226]
  SP1 = SPEAKER [package=pcb_mount_speaker]
  SP2 = SPEAKER [package=pcb_mount_speaker]
  Part9 = Arduino Nano (Rev3.0)
  S1 = Taiway 100-SP-X-T1 SPDT Miniature Toggle Switch [part_number=100-SP-X-T1-0-0-B1-M1 package=THT]
  S3 = Round Pushbutton
  S4 = Taiway 100-SP-X-T1 SPDT Miniature Toggle Switch [part_number=100-SP-X-T1-0-0-B1-M1 package=THT]
  S5 = Taiway 100-SP-X-T1 SPDT Miniature Toggle Switch [part_number=100-SP-X-T1-0-0-B1-M1 package=THT]
  Part10 = Adafruit Breadboard-Friendly NeoPixel [part_number="Adafruit #1312"]
  Part11 = Adafruit Breadboard-Friendly NeoPixel [part_number="Adafruit #1312"]
  Part12 = Adafruit Breadboard-Friendly NeoPixel [part_number="Adafruit #1312"]
  Part13 = Adafruit Breadboard-Friendly NeoPixel [part_number="Adafruit #1312"]
  Part14 = Adafruit Breadboard-Friendly NeoPixel [part_number="Adafruit #1312"]
  Part15 = Adafruit Breadboard-Friendly NeoPixel [part_number="Adafruit #1312"]
  Part16 = Adafruit Breadboard-Friendly NeoPixel [part_number="Adafruit #1312"]
  Part17 = Adafruit Breadboard-Friendly NeoPixel [part_number="Adafruit #1312"]
  Part18 = NeoPixel Jewel [part_number=2226]

nets (from the breadboard view):
  N1: MP1584EN_Board1.IN_-, MP1584EN_Board2.IN_-, U1.-
  N2: MP1584EN_Board1.IN_+, MP1584EN_Board2.IN_+, U1.+
  N3: MP1584EN_Board1.OUT_-, Part1.GND
  N4: MP1584EN_Board1.OUT_+, Part1.VDD
  GND: MP1584EN_Board2.OUT_-#13, Part2.GND, Part2.UG, Part1.IN_R_N, Part1.IN_L_N, Part3.GND, Part4.GND, Part5.GND, Part6.GND, Part7.GND, Part8.GND, Part9.GND, S1.L2, S3.leg0, S4.L2, S5.L2, Part10.GND, Part11.GND, Part12.GND, Part13.GND, Part14.GND, Part15.GND, Part16.GND, Part17.GND, Part18.GND
  VDD: MP1584EN_Board2.OUT_+, Part2.VIN, Part3.+5V, Part4.+5V, Part5.VDD, Part6.VDD, Part7.VDD, Part8.VDD, Part9.5V, Part10.VDD, Part11.VDD, Part12.VDD, Part13.VDD, Part14.VDD, Part15.VDD, Part16.VDD, Part17.VDD, Part18.VDD
  N5: Part2.TX, Part9.D11/MOSI
  N6: Part2.RX, Part9.D10
  N7: Part2.R, Part1.IN_R_P
  N8: Part2.L, Part1.IN_L_P
  N9: Part2.ACT, Part9.D12/MISO
  N10: Part2.RST, Part9.D9
  N11: Part1.OUT_L_N, SP2.-
  N12: Part1.OUT_L_P, SP2.+
  N13: Part1.OUT_R_P, SP1.+
  N14: Part1.OUT_R_N, SP1.-
  N15: Part3.DATAOUT, Part4.DATAIN
  N16: Part3.DATAIN, Part9.D2
  N17: Part4.DATAOUT, Part7.IN
  N18: Part5.IN, Part7.OUT
  N19: Part5.OUT, Part6.IN
  N20: Part6.OUT, Part8.IN
  N21: Part8.OUT, Part14.IN
  N22: Part9.D3, Part18.IN
  N23: Part9.D4, Part10.IN
  N24: Part9.D5, S4.L1
  N25: Part9.D6, S1.L1
  N26: Part9.D7, S5.L1
  N27: Part9.D8, S3.leg1
  N28: Part10.OUT, Part11.IN
  N29: Part11.OUT, Part12.IN
  N30: Part12.OUT, Part13.IN
  N31: Part14.OUT, Part15.IN
  N32: Part15.OUT, Part16.IN
  N33: Part16.OUT, Part17.IN

custom parts:
  MP1584EN Power Regulator Board: The MP1584EN is a high frequency step-down switching regulator. The input voltage range is 4.5V to 28V. The output voltage is set by the board's potentiometer.
  Audio FX Sound Board: The Adafruit Sound Board, the fastest way to add audio effects to a project!
  Adafruit Stereo 2.8W Class D Audio Amplifier - I2C Control AGC - TPA2016: A mini class D with AGC and I2C control? Yes please! This incredibly small stereo amplifier is surprisingly powerful. It is able to deliver 2 x 2.8W channels into 4 ohm impedance speakers (@ 10% THD) and it has a i2c control interface as well as an AGC (automatic gain control) system to keep your audio from clipping or distorting. If you don't want to use I2C to control it, it does start up on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
  NeoPixel Stick: Make your own little LED strip arrangement with this stick of NeoPixel LEDs. We crammed 8 of the tiny 5050 (5mm x 5mm) smart RGB LEDs onto a PCB with mounting holes and a chainable design. Use only one microcontroller pin to control as many as you can chain together! Each LED is addressable as the driver chip is inside the LED. Each one has ~18mA constant current drive so the color will be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
  NeoPixel Jewel: We fit seven of our tiny 5050 (5mm x 5mm) smart RGB LEDs onto a beautiful, round PCB with mounting holes and a chainable design to create what we think is our most elegant (and evening-wear appropriate) NeoPixel board yet. Use only one microcontroller pin to control as many as you can chain together! Each LED is addressable as the driver chip is inside the LED. Each one has ~18mA constant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
  Adafruit Breadboard-Friendly NeoPixel: This is the easiest way possible to add small, bright RGB pixels to your project. We took the same technology from our Flora NeoPixels and made them breadboard friendly, with two rows of 3 x 0.1" spaced header on each side for easy soldering, chaining and breadboarding. These ultra-bright LEDs have a constant-current driver cooked right into the LED package! The pixels are chainable - so you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
